# Fritzing sketch mic_sensor_MAX9812L (saved by Fritzing 0.9.3b)
breadboards: 1

parts:
  Componente1 = Arduino Uno (Rev3)
  Componente2 = Breakout Board for Electret Microphone

nets:
  N1: Componente1.A0, Componente2.VCC
  N2: Componente1.5V, Componente2.AUD
  GND: Componente1.GND, Componente2.GND

notes:
  MAX9812L: 2.7V to 3.6V
  MAX9812H: 4.5V to 5.5V

// code stored in the sketch: mic_sensor_MAX9812L.ino
const int sensorPIN = A0;
const int sampleWindow = 50; // Ancho ventana en mS (50 mS = 20Hz)
 
void setup() 
{
   Serial.begin(9600);
}
 
void loop() 
{
   unsigned long startMillis= millis();
 
   unsigned int signalMax = 0;
   unsigned int signalMin = 1024;
 
   // Recopilar durante la ventana
   unsigned int sample;
   while (millis() - startMillis < sampleWindow)
   {
      sample = analogRead(sensorPIN);
      if (sample < 1024)
      {
         if (sample > signalMax)
         {
            signalMax = sample;  // Actualizar máximo
         }
         else if (sample < signalMin)
         {
            signalMin = sample;  // Actualizar mínimo
         }
      }
   }
   unsigned int peakToPeak = signalMax - signalMin;  // Amplitud del sonido
   double volts = (peakToPeak * 5.0) / 1024;  // Convertir a tensión
   Serial.println(volts);
}
